# Fritzing sketch drifterElectronicsV2 2 (saved by Fritzing 0.9.9b)
stripboards: 1

parts:
  Part1 = Analog Digital MUX Breakout
  Part5 = Adafruit Adalogger FeatherWing [part_number="Adafruit #2922"]
  A3 = Honeywell 26pcxxh6d [package=THT]  # not connected
  DS4 = DS18B20 1-Wire Temperature Sensor [part_number=DS18B20]  # not connected
  DS5 = DS18B20 1-Wire Temperature Sensor [part_number=DS18B20]  # not connected
  DS6 = DS18B20 1-Wire Temperature Sensor [part_number=DS18B20]  # not connected
  A4 = Pololu DV24V50F5
  R9 = Temperature Sensor (Thermistor) [thermistor_type=NTC package=THT]
  R10 = Resistor [tolerance=±5% resistance=4.7k package="1206 [SMD]"]
  Part6 = Adafruit ESP32 Feather V2
  Part7 = Adafruit Ultimate GPS v3 [part_number="Adafruit #746"]  # not connected

nets:
  N1: Part1.GND, A4.Pin_3, A4.Pin_4
  N2: Part1.VCC, A4.Pin_5
  N3: Part1.S0, Part6.IO13_A12
  N4: Part1.S1, Part6.IO27_A10
  N5: Part1.S2, Part6.IO15_A8
  N6: Part1.S3, Part6.IO32_A7
  N7: Part1.SIG, Part6.IO14_A6
  N8: Part5.SCL, Part6.SCL
  N9: Part5.SCK, Part6.SCK
  N10: Part5.MOSI, Part6.MOSI
  N11: Part5.MISO, Part6.MISO
  N12: Part5.SDA, Part6.SDA
  N13: R9.pin_0, R10.Pin_0

notes:
  Red - (+) 5v
  Black - (-) 5V
  White - SCL or (+) sig
  Green - SDA or (-) sig
  Blue - MI
  Yellow - MO
  Grey - SCK
  Orange - CS
  Worth noting that the V regulator can be turned off with EN pin
  P33 is CS for SD card

custom parts:
  Adafruit Adalogger FeatherWing: This is the Adalogger FeatherWing: it adds both a battery-backed Real Time Clock and micro SD card storage to any Feather main board. This FeatherWing will make it real easy to add datalogging to any of our existing Feathers. You get both an I2C real time clock (PCF8523) with 32KHz crystal and battery backup, and a microSD socket that connects to the SPI port pins (+ extra pin for CS). Tested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
  Honeywell 26pcxxh6d: The 26PC Series Miniature Pressure Sensors are small, cost-effective devices intended for use with wet or dry media.
  Pololu DV24V50F5: This small synchronous switching step-down (or buck) regulator takes an input voltage of up to 38 V and efficiently reduces it to 5 V.
  Adafruit Ultimate GPS v3: We carry a few different GPS modules here in the Adafruit shop, but none that satisfied our every desire - that's why we designed this little GPS breakout board. We believe this is the Ultimate GPS module, so we named it that. It's got everything you want and more: -165 dBm sensitivity, 10 Hz updates, 66 channels 5V friendly design and only 20mA current draw Breadboard friendly + two mounting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
